// Logisim project control-logic.circ as structural Verilog: 1 circuit, main circuit control_logic
module control_logic (
  input  [31:0] inst,
  input  BrEq,
  input  BrLt,
  output PCSel,
  output RegWEn,
  output [2:0] ImmSel,
  output BrUn,
  output ASel,
  output BSel,
  output [3:0] ALUSel,
  output MemRW,
  output [1:0] WBSel,
  output CSRSel,
  output CSRWen
);

  wire add0, addi0, and7, and_1_out, comparator_3_eq, comparator_9_eq, comparator_10_eq, comparator_11_eq,
       comparator_12_eq, comparator_13_eq, comparator_14_eq, comparator_15_eq, comparator_18_eq,
       comparator_19_eq, comparator_21_eq, comparator_22_eq, comparator_23_eq, comparator_24_eq,
       comparator_25_eq, comparator_28_eq, comparator_29_eq, comparator_30_eq, comparator_33_eq, I_Type,
       is_jump, is_load, is_lui, mul8, mulh9, mulhu11, multiplexer_3_out, not_1_out, not_2_out, or6,
       or_2_out, R_Type, S_Type, SB_Type, sll1, slli1, slt2, sra13, srl5, sub12, U_Type, UJ_Type, xor4;
  wire [3:0] I_ALUSel, priority_encoder_1_out, R_ALUSel;

  Demultiplexer #(.enable("false"), .select(2)) demultiplexer_1 (
    .out0(add0), .out1(mul8), .out2(sub12), .in(addi0), .sel({inst[30], inst[25]}));  // open: out3
  Comparator #(.mode("unsigned"), .width(3)) comparator_1 (.a(inst[14:12]), .b(3'b000), .eq(addi0));  // open: gt, lt
  Demultiplexer #(.enable("false")) demultiplexer_2 (.out0(sll1), .out1(mulh9), .in(slli1), .sel(inst[25]));
  Comparator #(.mode("unsigned"), .width(3)) comparator_2 (.a(inst[14:12]), .b(3'b001), .eq(slli1));  // open: gt, lt
  Demultiplexer #(.enable("false")) demultiplexer_3 (.out0(srl5), .out1(sra13), .in(comparator_3_eq), .sel(inst[30]));
  Comparator #(.mode("unsigned"), .width(3)) comparator_3 (
    .a(inst[14:12]), .b(3'b101), .eq(comparator_3_eq));  // open: gt, lt
  Comparator #(.mode("unsigned"), .width(3)) comparator_4 (.a(inst[14:12]), .b(3'b011), .eq(mulhu11));  // open: gt, lt
  Comparator #(.mode("unsigned"), .width(3)) comparator_5 (.a(inst[14:12]), .b(3'b010), .eq(slt2));  // open: gt, lt
  Comparator #(.mode("unsigned"), .width(3)) comparator_6 (.a(inst[14:12]), .b(3'b100), .eq(xor4));  // open: gt, lt
  Comparator #(.mode("unsigned"), .width(3)) comparator_7 (.a(inst[14:12]), .b(3'b110), .eq(or6));  // open: gt, lt
  Comparator #(.mode("unsigned"), .width(3)) comparator_8 (.a(inst[14:12]), .b(3'b111), .eq(and7));  // open: gt, lt
  Multiplexer #(.enable("false"), .select(2), .width(4)) multiplexer_1 (
    .in0(4'b0000), .in1(R_ALUSel), .in2(I_ALUSel), .out(ALUSel), .sel({I_Type, R_Type}));  // open: in3
  Comparator #(.mode("unsigned"), .width(7)) comparator_9 (
    .a(inst[6:0]), .b(7'b0110011), .eq(comparator_9_eq));  // open: gt, lt
  Comparator #(.mode("unsigned"), .width(7)) comparator_10 (
    .a(inst[6:0]), .b(7'b0000011), .eq(comparator_10_eq));  // open: gt, lt
  Comparator #(.mode("unsigned"), .width(7)) comparator_11 (
    .a(inst[6:0]), .b(7'b0010011), .eq(comparator_11_eq));  // open: gt, lt
  Comparator #(.mode("unsigned"), .width(7)) comparator_12 (
    .a(inst[6:0]), .b(7'b0010111), .eq(comparator_12_eq));  // open: gt, lt
  Comparator #(.mode("unsigned"), .width(7)) comparator_13 (
    .a(inst[6:0]), .b(7'b0110111), .eq(comparator_13_eq));  // open: gt, lt
  Comparator #(.mode("unsigned"), .width(7)) comparator_14 (
    .a(inst[6:0]), .b(7'b1101111), .eq(comparator_14_eq));  // open: gt, lt
  Comparator #(.mode("unsigned"), .width(7)) comparator_15 (
    .a(inst[6:0]), .b(7'b1100111), .eq(comparator_15_eq));  // open: gt, lt
  or or_1 (RegWEn, comparator_9_eq, comparator_10_eq, comparator_11_eq, comparator_12_eq, comparator_13_eq, comparator_14_eq, comparator_15_eq);
  Priority_Encoder #(.select(4)) priority_encoder_1 (
    .in0(addi0), .in1(slli1), .in2(slt2), .in4(xor4), .in5(srl5), .in6(or6), .in7(and7), .in13(sra13),
    .out(priority_encoder_1_out));  // open: in3, in8, in9, in10, in11, in12, in14, in15, gs, en_out, en_in
  Priority_Encoder #(.select(4)) priority_encoder_2 (
    .in0(add0), .in1(sll1), .in2(slt2), .in4(xor4), .in5(srl5), .in6(or6), .in7(and7), .in8(mul8),
    .in9(mulh9), .in11(mulhu11), .in12(sub12), .in13(sra13), .out(R_ALUSel));  // open: in3, in10, in14, in15, gs, en_out, en_in
  Multiplexer #(.enable("false"), .width(4)) multiplexer_2 (
    .in0(4'b0000), .in1(priority_encoder_1_out), .out(I_ALUSel), .sel(inst[4]));
  Comparator #(.mode("unsigned"), .width(7)) comparator_16 (
    .a(inst[6:0]), .b(7'b1110011), .eq(CSRWen));  // open: gt, lt
  Comparator #(.mode("unsigned"), .width(7)) comparator_17 (.a(inst[6:0]), .b(7'b0100011), .eq(MemRW));  // open: gt, lt
  Priority_Encoder priority_encoder_3 (
    .in0(I_Type), .in1(S_Type), .in2(SB_Type), .in3(U_Type), .in4(UJ_Type), .out(ImmSel));  // open: in5, in6, in7, en_in, gs, en_out
  not not_1 (not_1_out, BrEq);
  not not_2 (not_2_out, BrLt);
  Multiplexer #(.enable("false"), .select(2)) multiplexer_3 (
    .in0(BrEq), .in1(not_1_out), .in2(BrLt), .in3(not_2_out), .out(multiplexer_3_out),
    .sel({inst[14], inst[12]}));
  Comparator #(.mode("unsigned"), .width(7)) comparator_18 (
    .a(inst[6:0]), .b(7'b0010011), .eq(comparator_18_eq));  // open: gt, lt
  Comparator #(.mode("unsigned"), .width(7)) comparator_19 (
    .a(inst[6:0]), .b(7'b0010111), .eq(comparator_19_eq));  // open: gt, lt
  Comparator #(.mode("unsigned"), .width(7)) comparator_20 (.a(inst[6:0]), .b(7'b0110011), .eq(BSel));  // open: gt, lt
  Comparator #(.mode("unsigned"), .width(7)) comparator_21 (
    .a(inst[6:0]), .b(7'b1100011), .eq(comparator_21_eq));  // open: gt, lt
  Comparator #(.mode("unsigned"), .width(7)) comparator_22 (
    .a(inst[6:0]), .b(7'b0010111), .eq(comparator_22_eq));  // open: gt, lt
  Comparator #(.mode("unsigned"), .width(7)) comparator_23 (
    .a(inst[6:0]), .b(7'b1101111), .eq(comparator_23_eq));  // open: gt, lt
  Comparator #(.mode("unsigned"), .width(7)) comparator_24 (
    .a(inst[6:0]), .b(7'b1100111), .eq(comparator_24_eq));  // open: gt, lt
  and and_1 (and_1_out, SB_Type, multiplexer_3_out);
  or or_2 (or_2_out, R_Type, comparator_18_eq, comparator_19_eq);
  or or_3 (ASel, comparator_21_eq, comparator_22_eq, comparator_23_eq, comparator_24_eq);
  or or_4 (PCSel, is_jump, and_1_out);
  Priority_Encoder #(.select(2)) priority_encoder_4 (
    .in0(or_2_out), .in1(is_load), .in2(is_lui), .in3(is_jump), .out(WBSel));  // open: gs, en_out, en_in
  Comparator #(.mode("unsigned"), .width(7)) comparator_25 (
    .a(inst[6:0]), .b(7'b1100111), .eq(comparator_25_eq));  // open: gt, lt
  Comparator #(.mode("unsigned"), .width(7)) comparator_26 (
    .a(inst[6:0]), .b(7'b0110011), .eq(R_Type));  // open: gt, lt
  Comparator #(.mode("unsigned"), .width(7)) comparator_27 (
    .a(inst[6:0]), .b(7'b0000011), .eq(is_load));  // open: gt, lt
  Comparator #(.mode("unsigned"), .width(7)) comparator_28 (
    .a(inst[6:0]), .b(7'b0010011), .eq(comparator_28_eq));  // open: gt, lt
  Comparator #(.mode("unsigned"), .width(7)) comparator_29 (
    .a(inst[6:0]), .b(7'b1100111), .eq(comparator_29_eq));  // open: gt, lt
  Comparator #(.mode("unsigned"), .width(7)) comparator_30 (
    .a(inst[6:0]), .b(7'b1110011), .eq(comparator_30_eq));  // open: gt, lt
  Comparator #(.mode("unsigned"), .width(7)) comparator_31 (
    .a(inst[6:0]), .b(7'b0100011), .eq(S_Type));  // open: gt, lt
  Comparator #(.mode("unsigned"), .width(7)) comparator_32 (
    .a(inst[6:0]), .b(7'b1100011), .eq(SB_Type));  // open: gt, lt
  Comparator #(.mode("unsigned"), .width(7)) comparator_33 (
    .a(inst[6:0]), .b(7'b0010111), .eq(comparator_33_eq));  // open: gt, lt
  Comparator #(.mode("unsigned"), .width(7)) comparator_34 (
    .a(inst[6:0]), .b(7'b0110111), .eq(is_lui));  // open: gt, lt
  Comparator #(.mode("unsigned"), .width(7)) comparator_35 (
    .a(inst[6:0]), .b(7'b1101111), .eq(UJ_Type));  // open: gt, lt
  or or_5 (is_jump, UJ_Type, comparator_25_eq);
  or or_6 (I_Type, is_load, comparator_28_eq, comparator_29_eq, comparator_30_eq);
  or or_7 (U_Type, comparator_33_eq, is_lui);

  assign BrUn = inst[13];
  assign CSRSel = inst[14];

  // Other names for the same wires on the sheet: opcode[6:0] = inst[6:0]; is_arithmetic = inst[4];
  //   funct3[2:0] = inst[14:12]; bit25 = inst[25]; funct7[6:0] = inst[31:25]; bit30 = inst[30]

  // Notes on the sheet:
  //   R-Type
  //   I-Type (loads)
  //   I-Type (arithmetic)
  //   auipc
  //   lui
  //   jal
  //   jalr
  //   INPUTS to your circuit
  //   DON'T CHANGE THE LOCATIONS OF THE INPUTS AND OUTPUTS!
  //   OUTPUT from your circuit
endmodule
