// Logisim project cpu.circ as structural Verilog: 1 circuit, main circuit cpu
module cpu (
  input  clk,
  input  [31:0] INSTRUCTION,
  input  [31:0] READ_DATA,
  output [31:0] WRITE_ADDRESS,
  output [31:0] PROGRAM_COUNTER,
  output [31:0] ra,
  output [31:0] sp,
  output [31:0] t0,
  output [31:0] t1,
  output [31:0] t2,
  output [31:0] s0,
  output [31:0] s1,
  output [31:0] a0,
  output [31:0] tohost,
  output [3:0] WRITE_ENABLE,
  output [31:0] WRITE_DATA
);

  wire alu_1_p2, alu_1_p6, alu_1_p10, ASel, BrEq, BrLt, BrUn, BSel, CSR_WE, CSRSel, MemRW, PCSel,
       regfile_1_p1, regfile_1_p9, regfile_1_p11, regfile_1_p23, regfile_1_p25, regfile_1_p27, RegWEn;
  wire [1:0] bit_extender_4_out, bit_extender_5_out, bit_extender_7_out, bit_extender_8_out,
       bit_extender_9_out, MemSel, WBSel;
  wire [2:0] ImmSel;
  wire [3:0] ALUOp, bit_extender_12_out, multiplexer_9_out, shifter_2_out, shifter_3_out;
  wire [4:0] and_1_out, bit_extender_3_out, shifter_1_out;
  wire [7:0] bit_extender_6_out, demultiplexer_1_out0, demultiplexer_1_out1, demultiplexer_1_out2,
       demultiplexer_1_out3, multiplexer_7_out;
  wire [11:0] bit_extender_2_out;
  wire [15:0] multiplexer_8_out;
  wire [31:0] adder_1_out, and_2_out, bit_extender_1_out, bit_extender_10_out, bit_extender_11_out, EX_INST,
       EX_PC, imm, LOAD_DATA, multiplexer_1_out, multiplexer_2_out, multiplexer_3_out, multiplexer_4_out,
       multiplexer_5_out, multiplexer_6_out, regfile_1_p20, shifter_4_out, ToWrite;

  Adder #(.width(32)) adder_1 (.a(PROGRAM_COUNTER), .b(32'h4), .out(adder_1_out));  // open: cin, cout
  Register #(.width(32)) register_1 (.D(multiplexer_1_out), .clk(clk), .Q(EX_INST));  // open: en, clr
  Multiplexer #(.enable("false"), .width(32)) multiplexer_1 (
    .in0(INSTRUCTION), .in1(32'h13), .out(multiplexer_1_out), .sel(PCSel));
  Multiplexer #(.enable("false"), .width(32)) multiplexer_2 (
    .in0(adder_1_out), .in1(WRITE_ADDRESS), .out(multiplexer_2_out), .sel(PCSel));
  control_logic control_logic_1 (
    .CSRWen(CSR_WE), .PCSel(PCSel), .RegWEn(RegWEn), .ImmSel(ImmSel), .BrUn(BrUn), .ASel(ASel), .BSel(BSel),
    .ALUSel(ALUOp), .MemRW(MemRW), .WBSel(WBSel), .CSRSel(CSRSel), .inst(EX_INST), .BrEq(BrEq), .BrLt(BrLt));
  Register #(.width(32)) PC (.D(multiplexer_2_out), .clk(clk), .Q(PROGRAM_COUNTER));  // open: en, clr
  Register #(.width(32)) register_2 (.D(PROGRAM_COUNTER), .clk(clk), .Q(EX_PC));  // open: en, clr
  imm_gen imm_gen_1 (.inst(EX_INST), .ImmSel(ImmSel), .imm(imm));
  Multiplexer #(.enable("false"), .select(2), .width(32)) multiplexer_3 (
    .in0(WRITE_ADDRESS), .in1(LOAD_DATA), .in2(imm), .in3(PROGRAM_COUNTER), .out(multiplexer_3_out),
    .sel(WBSel));
  // regfile regfile_1: pin names not known; wires that end beside it: regfile_1_p1, EX_INST[19:15], EX_INST[24:20], EX_INST[11:7], multiplexer_3_out, RegWEn, clk, regfile_1_p1, regfile_1_p9, regfile_1_p9, regfile_1_p11, ra, sp, t0, t1, t2, s0, s1, a0, regfile_1_p20, ToWrite, regfile_1_p11, regfile_1_p23, regfile_1_p23, regfile_1_p25, regfile_1_p25, regfile_1_p27
  branch_comp branch_comp_1 (.rs1(regfile_1_p20), .rs2(ToWrite), .BrUn(BrUn), .BrEq(BrEq), .BrLt(BrLt));
  assign bit_extender_1_out = {{27{EX_INST[19]}}, EX_INST[19:15]};  // Bit_Extender bit_extender_1
  Bit_Extender #(.in_width(32), .out_width(12)) bit_extender_2 (.in(imm), .out(bit_extender_2_out));
  Multiplexer #(.enable("false"), .width(32)) multiplexer_4 (
    .in0(regfile_1_p20), .in1(bit_extender_1_out), .out(multiplexer_4_out), .sel(CSRSel));
  Multiplexer #(.enable("false"), .width(32)) multiplexer_5 (
    .in0(regfile_1_p20), .in1(EX_PC), .out(multiplexer_5_out), .sel(ASel));
  Multiplexer #(.enable("false"), .width(32)) multiplexer_6 (
    .in0(imm), .in1(ToWrite), .out(multiplexer_6_out), .sel(BSel));
  // csr csr_1: pin names not known; wires that end beside it: bit_extender_2_out, multiplexer_4_out, CSR_WE, clk, tohost
  // alu alu_1: pin names not known; wires that end beside it: regfile_1_p27, alu_1_p2, alu_1_p2, multiplexer_5_out, multiplexer_6_out, alu_1_p6, ALUOp, alu_1_p6, WRITE_ADDRESS, alu_1_p10
  Bit_Extender #(.in_width(32), .out_width(5), .\type ("zero")) bit_extender_3 (
    .in(WRITE_ADDRESS), .out(bit_extender_3_out));
  Bit_Extender #(.in_width(32), .out_width(2), .\type ("zero")) bit_extender_4 (
    .in(WRITE_ADDRESS), .out(bit_extender_4_out));
  Bit_Extender #(.in_width(32), .out_width(2), .\type ("zero")) bit_extender_5 (
    .in(WRITE_ADDRESS), .out(bit_extender_5_out));
  Bit_Extender #(.in_width(32), .out_width(8), .\type ("zero")) bit_extender_6 (.in(ToWrite), .out(bit_extender_6_out));
  assign and_1_out = 5'b00011 & bit_extender_3_out;  // AND_Gate and_1, 5 bits wide
  Shifter #(.width(5)) shifter_1 (.in(and_1_out), .\dist (3'b011), .out(shifter_1_out));
  Shifter #(.width(4)) shifter_2 (.in(4'b0001), .\dist (bit_extender_4_out), .out(shifter_2_out));
  Shifter #(.width(4)) shifter_3 (.in(4'b0011), .\dist (bit_extender_5_out), .out(shifter_3_out));
  Multiplexer #(.enable("false"), .select(2), .width(8)) multiplexer_7 (
    .in0(READ_DATA[7:0]), .in1(READ_DATA[15:8]), .in2(READ_DATA[23:16]), .in3(READ_DATA[31:24]),
    .out(multiplexer_7_out), .sel(bit_extender_7_out));
  Bit_Extender #(.in_width(32), .out_width(2), .\type ("zero")) bit_extender_7 (
    .in(WRITE_ADDRESS), .out(bit_extender_7_out));
  Multiplexer #(.enable("false"), .select(2), .width(16)) multiplexer_8 (
    .in0(READ_DATA[15:0]), .in1(READ_DATA[23:8]), .in2(READ_DATA[31:16]), .out(multiplexer_8_out),
    .sel(bit_extender_8_out));  // open: in3
  Bit_Extender #(.in_width(32), .out_width(2), .\type ("zero")) bit_extender_8 (
    .in(WRITE_ADDRESS), .out(bit_extender_8_out));
  Demultiplexer #(.enable("false"), .select(2), .width(8)) demultiplexer_1 (
    .out0(demultiplexer_1_out0), .out1(demultiplexer_1_out1), .out2(demultiplexer_1_out2),
    .out3(demultiplexer_1_out3), .in(bit_extender_6_out), .sel(bit_extender_9_out));
  Bit_Extender #(.in_width(32), .out_width(2), .\type ("zero")) bit_extender_9 (
    .in(WRITE_ADDRESS), .out(bit_extender_9_out));
  assign and_2_out = 32'hffff & ToWrite;  // AND_Gate and_2, 32 bits wide
  Multiplexer #(.enable("false"), .select(2), .width(4)) multiplexer_9 (
    .in0(shifter_2_out), .in1(shifter_3_out), .in2(4'b1111), .out(multiplexer_9_out), .sel(MemSel));  // open: in3
  assign bit_extender_10_out = {{24{multiplexer_7_out[7]}}, multiplexer_7_out};  // Bit_Extender bit_extender_10
  assign bit_extender_11_out = {{16{multiplexer_8_out[15]}}, multiplexer_8_out};  // Bit_Extender bit_extender_11
  Shifter #(.width(32)) shifter_4 (.in(and_2_out), .\dist (shifter_1_out), .out(shifter_4_out));
  assign bit_extender_12_out = {{3{MemRW}}, MemRW};  // Bit_Extender bit_extender_12
  assign WRITE_ENABLE = bit_extender_12_out & multiplexer_9_out;  // AND_Gate and_3, 4 bits wide
  Multiplexer #(.enable("false"), .select(2), .width(32)) multiplexer_10 (
    .in0(bit_extender_10_out), .in1(bit_extender_11_out), .in2(READ_DATA), .out(LOAD_DATA), .sel(MemSel));  // open: in3
  Multiplexer #(.enable("false"), .select(2), .width(32)) multiplexer_11 (
    .in0({demultiplexer_1_out3, demultiplexer_1_out2, demultiplexer_1_out1, demultiplexer_1_out0}),
    .in1(shifter_4_out), .in2(ToWrite), .out(WRITE_DATA), .sel(MemSel));  // open: in3

  // Other names for the same wires on the sheet: ALURes[31:0] = WRITE_ADDRESS; FE_INST[31:0] = INSTRUCTION;
  //   FE_PC[31:0] = PROGRAM_COUNTER

  // Notes on the sheet:
  //   Output to IMEM
  //   IMEM (do **NOT** move this)
  //   Inputs from IMEM
  //   Inputs/Outputs for testing. Do **NOT** move these.
  //   Outputs To DMEM
  //   DMEM (do **NOT** move this)
  //   Inputs From DMEM
endmodule
